// Logisim project Basic_Computer.circ as structural Verilog: 5 circuits, main circuit main
module main (
  input  in_1,
  input  in_2,
  input  in_3,
  output [2:0] out_4,
  output out_5,
  output out_6,
  output [15:0] out_7,
  output [2:0] out_8
);

  wire clock_1_out, control_unit_1_ac, control_unit_1_ar, control_unit_1_dr, control_unit_1_ir,
       control_unit_1_pc, control_unit_1_pc_inr, control_unit_1_read, control_unit_1_write;
  wire [11:0] AR_q, bit_extender_1_out, bit_extender_2_out, PC_q;
  wire [15:0] AC_q, alu_1_alu_output, bit_extender_3_out, bit_extender_4_out, DR_q, IR_q, ram_1_data, TR_q;

  Clock clock_1 (.out(clock_1_out));
  Control_Unit control_unit_1 (
    .IR_Content(IR_q), .AC_Content(AC_q), .Bus_Selection_Lines(out_8), .PC(control_unit_1_pc),
    .IR(control_unit_1_ir), .PC_INR(control_unit_1_pc_inr), .AR(control_unit_1_ar), .DR(control_unit_1_dr),
    .AC(control_unit_1_ac), .ALU(out_4), .Write(control_unit_1_write), .Read(control_unit_1_read),
    .clock(clock_1_out));
  Bit_Extender #(.in_width(16), .out_width(12)) bit_extender_1 (.in(out_7), .out(bit_extender_1_out));
  Bit_Extender #(.in_width(16), .out_width(12)) bit_extender_2 (.in(out_7), .out(bit_extender_2_out));
  Register #(.width(16)) AC (.D(alu_1_alu_output), .en(control_unit_1_ac), .Q(AC_q), .clk(clock_1_out));  // open: clr
  Register #(.width(16)) DR (.D(out_7), .en(control_unit_1_dr), .Q(DR_q), .clk(clock_1_out));  // open: clr
  Register #(.width(12)) AR (.D(bit_extender_1_out), .en(control_unit_1_ar), .Q(AR_q), .clk(clock_1_out));  // open: clr
  Register #(.width(16)) TR (.D(out_7), .en(in_3), .Q(TR_q), .clk(clock_1_out));  // open: clr
  Counter #(.width(12), .max('hfff)) PC (
    .load(control_unit_1_pc), .D(bit_extender_2_out), .count(control_unit_1_pc_inr), .Q(PC_q),
    .clk(clock_1_out));  // open: carry, clr
  Register #(.width(16)) IR (.D(out_7), .en(control_unit_1_ir), .Q(IR_q), .clk(clock_1_out));  // open: clr
  RAM #(.addrWidth(12), .dataWidth(16), .bus("separate")) ram_1 (
    .addr(AR_q), .din(out_7), .data(ram_1_data), .str(control_unit_1_write), .clk(clock_1_out),
    .ld(control_unit_1_read));  // open: sel, clr
  ALU alu_1 (
    .in_1(in_1), .Input_1__AC(AC_q), .Input_2__DR(DR_q), .in_4(in_2), .Selection_of_ALU(out_4),
    .out_6(out_5), .out_7(out_6), .ALU_Output(alu_1_alu_output));
  assign bit_extender_3_out = {{4{1'b0}}, PC_q};  // Bit_Extender bit_extender_3
  assign bit_extender_4_out = {{4{1'b0}}, AR_q};  // Bit_Extender bit_extender_4
  Multiplexer #(.select(3), .width(16)) multiplexer_1 (
    .in0(AC_q), .in1(DR_q), .in2(TR_q), .in3(bit_extender_4_out), .in4(ram_1_data), .in5(bit_extender_3_out),
    .in6(IR_q), .out(out_7), .sel(out_8), .en(1'b1));  // open: in7

  // Notes on the sheet:
  //   PC
endmodule

module ALU (
  input  in_1,
  input  [15:0] Input_1__AC,
  input  [15:0] Input_2__DR,
  input  in_4,
  input  [2:0] Selection_of_ALU,
  output out_6,
  output out_7,
  output [15:0] ALU_Output
);

  wire [15:0] adder_1_out, and_1_out, Complement_AC__DR_is_also_correct_out, or_1_out, subtractor_1_out,
       xor_1_out;

  Adder #(.width(16)) adder_1 (.a(Input_1__AC), .b(Input_2__DR), .out(adder_1_out), .cin(in_1), .cout(out_6));
  Subtractor #(.width(16)) subtractor_1 (
    .a(Input_1__AC), .b(Input_2__DR), .out(subtractor_1_out), .bin(in_4), .bout(out_7));
  assign and_1_out = Input_1__AC & Input_2__DR;  // AND_Gate and_1, 16 bits wide
  assign or_1_out = Input_1__AC | Input_2__DR;  // OR_Gate or_1, 16 bits wide
  assign xor_1_out = Input_1__AC ^ Input_2__DR;  // XOR_Gate xor_1, 16 bits wide
  assign Complement_AC__DR_is_also_correct_out = ~Input_1__AC;  // NOT_Gate Complement_AC__DR_is_also_correct, 16 bits wide
  Multiplexer #(.select(3), .width(16)) multiplexer_1 (
    .in0(adder_1_out), .in1(subtractor_1_out), .in2(Input_2__DR), .in3(and_1_out), .in4(or_1_out),
    .in5(xor_1_out), .in6(Complement_AC__DR_is_also_correct_out), .out(ALU_Output), .sel(Selection_of_ALU),
    .en(1'b1));  // open: in7
endmodule

module Control_Unit (
  input  [15:0] IR_Content,
  input  [15:0] AC_Content,
  input  clock,
  output [2:0] Bus_Selection_Lines,
  output PC,
  output IR,
  output PC_INR,
  output AR,
  output DR,
  output AC,
  output [2:0] ALU,
  output Write,
  output Read
);

  wire d_ff_1_q, decoder_1_out0, decoder_1_out1, decoder_1_out2, decoder_1_out3, decoder_1_out4,
       decoder_1_out5, decoder_2_out0, decoder_2_out1, decoder_2_out2, decoder_2_out3, decoder_2_out4,
       decoder_2_out5, decoder_2_out7, SC_Clear_out_12;
  wire [3:0] counter_1_q;

  Control_Logic_Unit control_logic_unit_1 (
    .T0(decoder_1_out0), .T1(decoder_1_out1), .T2(decoder_1_out2), .T3(decoder_1_out3), .T4(decoder_1_out4),
    .T5(decoder_1_out5), .D0(decoder_2_out0), .D1(decoder_2_out1), .D2(decoder_2_out2), .D3(decoder_2_out3),
    .D4(decoder_2_out4), .D5(decoder_2_out5), .D7(decoder_2_out7), .I(1'b0), .B2(IR_Content[2]),
    .AC_Content(AC_Content), .Read(Read), .Write(Write), .ALU(ALU), .AC(AC), .DR(DR), .AR(AR),
    .PC_INR(PC_INR), .IR(IR), .PC(PC), .BUS_Selection_Lines(Bus_Selection_Lines));
  Counter #(.width(4), .max('hf)) counter_1 (
    .Q(counter_1_q), .clk(clock), .clr(d_ff_1_q));  // open: load, D, count, carry
  Decoder #(.select(4)) decoder_1 (
    .out0(decoder_1_out0), .out1(decoder_1_out1), .out2(decoder_1_out2), .out3(decoder_1_out3),
    .out4(decoder_1_out4), .out5(decoder_1_out5), .sel(counter_1_q), .en(1'b1));  // open: out6, out7, out8, out9, out10, out11, out12, out13, out14, out15
  Decoder #(.select(3)) decoder_2 (
    .out0(decoder_2_out0), .out1(decoder_2_out1), .out2(decoder_2_out2), .out3(decoder_2_out3),
    .out4(decoder_2_out4), .out5(decoder_2_out5), .out7(decoder_2_out7), .sel(IR_Content[14:12]), .en(1'b1));  // open: out6
  D_Flip_Flop d_ff_1 (.clk(clock), .D(SC_Clear_out_12), .Q(d_ff_1_q));  // open: Qn, preset, en, reset
  Clear_SC SC_Clear (
    .D0(decoder_2_out0), .D1(decoder_2_out1), .D2(decoder_2_out2), .D3(decoder_2_out3), .D4(decoder_2_out4),
    .D5(decoder_2_out5), .D7(decoder_2_out7), .I(1'b0), .T3(decoder_1_out3), .T4(decoder_1_out4),
    .T5(decoder_1_out5), .out_12(SC_Clear_out_12));
endmodule

module Clear_SC (
  input  D0,
  input  D1,
  input  D2,
  input  D3,
  input  D4,
  input  D5,
  input  D7,
  input  I,
  input  T3,
  input  T4,
  input  T5,
  output out_12
);

  wire and_1_out, and_2_out, and_3_out, and_4_out, and_5_out, and_6_out, and_7_out, not_1_out;

  not not_1 (not_1_out, I);
  and and_1 (and_1_out, D0, T5);
  and and_2 (and_2_out, D1, T5);
  and and_3 (and_3_out, D2, T5);
  and and_4 (and_4_out, D3, T4);
  and and_5 (and_5_out, D4, T4);
  and and_6 (and_6_out, D5, T5);
  and and_7 (and_7_out, D7, not_1_out, T3);
  or or_1 (out_12, and_1_out, and_2_out, and_3_out, and_4_out, and_5_out, and_6_out, and_7_out);
endmodule

module Control_Logic_Unit (
  input  T0,
  input  T1,
  input  T2,
  input  T3,
  input  T4,
  input  T5,
  input  D0,
  input  D1,
  input  D2,
  input  D3,
  input  D4,
  input  D5,
  input  D7,
  input  I,
  input  B2,
  input  [15:0] AC_Content,
  output Read,
  output Write,
  output [2:0] ALU,
  output AC,
  output DR,
  output AR,
  output PC_INR,
  output IR,
  output PC,
  output [2:0] BUS_Selection_Lines
);

  wire and_1_out, and_5_out, and_6_out, comparator_1_eq, controlled_buffer_1_out, not_1_out, not_2_out,
       or_3_out, or_4_out;
  wire [1:0] priority_encoder_1_out;

  not not_1 (not_1_out, I);
  or or_1 (AR, T0, T2);
  assign controlled_buffer_1_out = not_2_out ? 1'b0 : 1'bz;  // Controlled_Buffer controlled_buffer_1
  not not_2 (not_2_out, and_1_out);
  and and_1 (and_1_out, T3, D7, B2, not_1_out);
  Comparator #(.width(16)) comparator_1 (.a(AC_Content), .b({16{1'b0}}), .eq(comparator_1_eq));  // open: gt, lt
  and and_2 (Write, T4, D3);
  and and_3 (PC, T4, D4);
  assign controlled_buffer_1_out = and_1_out ? comparator_1_eq : 1'bz;  // Controlled_Buffer controlled_buffer_2
  or or_2 (PC_INR, T1, controlled_buffer_1_out);
  or or_3 (or_3_out, D0, D1, D2, D5);
  or or_4 (or_4_out, D0, D1, D2, D5);
  and and_4 (DR, T4, or_3_out);
  and and_5 (and_5_out, T5, or_4_out);
  and and_6 (and_6_out, D2, T5);
  or or_5 (Read, T1, DR);
  and and_7 (AC, T5, or_3_out);
  Priority_Encoder #(.select(2)) priority_encoder_1 (
    .in0(D1), .in1(D5), .in2(D2), .in3(D0), .out(priority_encoder_1_out), .en_in(and_5_out));  // open: gs, en_out
  assign ALU = {{1{1'b0}}, priority_encoder_1_out};  // Bit_Extender bit_extender_1
  Priority_Encoder priority_encoder_2 (
    .in0(Write), .in1(and_6_out), .in3(PC), .in4(Read), .in5(T0), .in6(T2), .out(BUS_Selection_Lines));  // open: in2, in7, en_in, gs, en_out

  assign IR = T1;
endmodule
